# Fritzing sketch LoRaRadioRXClientHardware (saved by Fritzing 0.9.3b)

parts:
  Part1 = Adafruit RFM9x LoRa Radio [part_number="Adafruit #3072 and #3073"]
  Part2 = Arduino Uno (Rev3)
  ANT1 = Antenna

nets:
  N1: Part1.ANTENNA, ANT1.antenna_lead
  VIN: Part1.VIN, Part2.5V
  GND: Part1.GND, Part2.GND
  N2: Part1.DIO0, Part2.D2
  N3: Part1.SCK, Part2.D13/SCK
  N4: Part1.MISO, Part2.D12/MISO
  N5: Part1.MOSI, Part2.D11_PWM/MOSI
  N6: Part1.CS, Part2.D10_PWM/SS
  N7: Part1.RST, Part2.D9_PWM

custom parts:
  Adafruit RFM9x LoRa Radio: Sending data over long distances is like magic, and now you can be a magician with this range of powerful and easy-to-use radio modules. Sure, sometimes you want to talk to a computer (a good time to use WiFi) or perhaps communicate with a Phone (choose Bluetooth Low Energy!) but what if you want to send data very far? Most WiFi, Bluetooth, Zigbee and other wireless chipsets use 2.4GHz, which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
